# Fritzing sketch circuit (saved by Fritzing 0.9.3b)
breadboards: 1

parts:
  IC1 = IC, DIP package, 14 pins [chip_label=LMC6484]
  C1 = Ceramic Capacitor [capacitance=100nF package="100 mil [THT, multilayer]"]
  12V_input = Power plug
  R1 = Resistor [tolerance=±1% resistance=10k package=THT]
  R3 = Resistor [tolerance=±1% resistance=56k package=THT]
  R4 = Resistor [tolerance=±1% resistance=10k package=THT]
  R5 = Resistor [tolerance=±1% resistance=10k package=THT]
  R6 = Resistor [tolerance=±1% resistance=10k package=THT]
  Bauteil1 = Arduino Nano (Rev3.0)

nets:
  N1: IC1.pin4, 12V_input.VCC
  N2: IC1.pin8, C1.1, R5.Pin_1
  N3: IC1.pin9, C1.0, R3.Pin_0
  N4: IC1.pin10, R1.Pin_1, R4.Pin_0
  GND: IC1.pin11, 12V_input.GND, R1.Pin_0, R6.Pin_0, Bauteil1.GND
  N5: R3.Pin_1, Bauteil1.D7
  N6: R4.Pin_1, Bauteil1.VIN
  N7: R5.Pin_0, R6.Pin_1, Bauteil1.A0
